// Logisim project t1.circ as structural Verilog: 5 circuits, main circuit main
module main (
);

  CLA_16bit cla_16bit_1 ();  // open: Cin, A, B, S, PG, GG, Cout, overflow
endmodule

module adder_1bit (
  input  C,
  input  A,
  input  B,
  output S,
  output P,
  output G
);

  xor xor_1 (P, A, B);
  xor xor_2 (S, C, P);
  and and_1 (G, A, B);
endmodule

module CLU_4in (
  input  C0,
  input  P0,
  input  P1,
  input  P2,
  input  P3,
  input  G0,
  input  G1,
  input  G2,
  input  G3,
  output C1,
  output C2,
  output C3,
  output C4,
  output PG,
  output GG,
  output overflow
);

  wire and_1_out, and_2_out, and_3_out, and_4_out, and_5_out, and_6_out, and_8_out, and_9_out, and_10_out,
       and_11_out;

  and and_1 (and_1_out, C0, P0);
  or or_1 (C1, and_1_out, G0);
  and and_2 (and_2_out, C0, P0, P1);
  and and_3 (and_3_out, G0, P1);
  or or_2 (C2, and_2_out, and_3_out, G1);
  and and_4 (and_4_out, C0, P0, P1, P2);
  and and_5 (and_5_out, G0, P1, P2);
  and and_6 (and_6_out, G1, P2);
  or or_3 (C3, and_4_out, and_5_out, and_6_out, G2);
  and and_7 (PG, P0, P1, P2, P3);
  and and_8 (and_8_out, G0, P1, P2, P3);
  and and_9 (and_9_out, G1, P2, P3);
  and and_10 (and_10_out, G2, P3);
  xor xor_1 (overflow, C4, C3);
  or or_4 (GG, and_8_out, and_9_out, and_10_out, G3);
  and and_11 (and_11_out, C0, PG);
  or or_5 (C4, and_11_out, GG);

  // Notes on the sheet:
  //   Carry 1
  //   Carry 2
  //   Carry 3
endmodule

module CLA_4bit (
  input  Cin,
  input  [3:0] A,
  input  [3:0] B,
  output [3:0] S,
  output PG,
  output GG,
  output Cout,
  output overflow
);

  wire C1, C2, C3, G0, G1, G2, G3, P0, P1, P2, P3;

  adder_1bit adder_1bit_1 (.C(Cin), .A(A[0]), .B(B[0]), .S(S[0]), .P(P0), .G(G0));
  adder_1bit adder_1bit_2 (.C(C1), .A(A[1]), .B(B[1]), .S(S[1]), .P(P1), .G(G1));
  adder_1bit adder_1bit_3 (.C(C2), .A(A[2]), .B(B[2]), .S(S[2]), .P(P2), .G(G2));
  adder_1bit adder_1bit_4 (.C(C3), .A(A[3]), .B(B[3]), .S(S[3]), .P(P3), .G(G3));
  CLU_4in clu_4in_1 (
    .C0(Cin), .P0(P0), .P1(P1), .P2(P2), .P3(P3), .G0(G0), .G1(G1), .G2(G2), .G3(G3), .C1(C1), .C2(C2),
    .C3(C3), .C4(Cout), .PG(PG), .GG(GG), .overflow(overflow));

  // Other names for the same wires on the sheet: C4 = Cout
endmodule

module CLA_16bit (
  input  Cin,
  input  [15:0] A,
  input  [15:0] B,
  output [15:0] S,
  output PG,
  output GG,
  output Cout,
  output overflow
);

  wire C1, C2, C3, G0, G1, G2, G3, P0, P1, P2, P3;

  // CLA_4bit cla_4bit_1: pin names not known; wires that end beside it: Cin, A[3:0], B[3:0], S[3:0], P0, G0
  // CLA_4bit cla_4bit_2: pin names not known; wires that end beside it: C1, A[7:4], B[7:4], S[7:4], P1, G1
  // CLA_4bit cla_4bit_3: pin names not known; wires that end beside it: C2, A[11:8], B[11:8], S[11:8], P2, G2
  // CLA_4bit cla_4bit_4: pin names not known; wires that end beside it: C3, A[15:12], B[15:12], S[15:12], P3, G3
  CLU_4in clu_4in_1 (
    .C0(Cin), .P0(P0), .P1(P1), .P2(P2), .P3(P3), .G0(G0), .G1(G1), .G2(G2), .G3(G3), .C1(C1), .C2(C2),
    .C3(C3), .C4(Cout), .PG(PG), .GG(GG), .overflow(overflow));

  // Other names for the same wires on the sheet: A0[3:0] = A[3:0]; A1[3:0] = A[7:4]; A2[3:0] = A[11:8];
  //   A3[3:0] = A[15:12]; B0[3:0] = B[3:0]; B1[3:0] = B[7:4]; B2[3:0] = B[11:8]; B3[3:0] = B[15:12]; C4 = Cout;
  //   S0[3:0] = S[3:0]; S1[3:0] = S[7:4]; S2[3:0] = S[11:8]; S3[3:0] = S[15:12]
endmodule
