// Logisim project t2.circ as structural Verilog: 5 circuits, main circuit main
module main (
  input  msg_bit,
  input  [31:0] polyn,
  input  load_polyn,
  input  clk,
  input  R,
  output [31:0] out_6,
  output [31:0] out_7
);

  wire button_1_out;
  wire [31:0] register_1_q;

  Register #(.width(32)) register_1 (.D(polyn), .en(1'b1), .clk(load_polyn), .Q(register_1_q), .clr(1'b0));
  count_32bit count_32bit_1 (.clk(clk), .R(R), .out_3(out_7));  // open: count_out
  Button button_1 (.out(button_1_out));
  calc calc_1 (.\bit (msg_bit), .G(register_1_q), .WE(1'b1), .clk(button_1_out), .D(out_6));  // open: R
endmodule

module bit_push (
  input  \bit ,
  input  [31:0] value,
  output [31:0] value_out
);


  assign value_out = {value[30:0], \bit };
endmodule

module calc (
  input  \bit ,
  input  [31:0] G,
  input  WE,
  input  clk,
  input  R,
  output [31:0] D
);

  wire [31:0] bit_push_1_value_out, multiplexer_1_out, xor_1_out;

  Register #(.width(32)) register_1 (.D(multiplexer_1_out), .en(WE), .clk(clk), .Q(D), .clr(R));
  assign xor_1_out = G ^ D;  // XOR_Gate xor_1, 32 bits wide
  bit_push bit_push_1 (.\bit (\bit ), .value(D), .value_out(bit_push_1_value_out));
  Multiplexer #(.width(32), .enable("false")) multiplexer_1 (
    .in0(bit_push_1_value_out), .in1(xor_1_out), .out(multiplexer_1_out), .sel(D[31]));
endmodule

module count_8bit (
  input  clk,
  input  R,
  output [7:0] value,
  output count_out
);

  wire t_ff_1_qn, t_ff_2_qn, t_ff_3_qn, t_ff_4_qn, t_ff_5_qn, t_ff_6_qn, t_ff_7_qn;

  T_Flip_Flop t_ff_1 (.T(1'b1), .clk(clk), .Q(value[0]), .Qn(t_ff_1_qn), .reset(R));  // open: preset
  T_Flip_Flop t_ff_2 (.T(1'b1), .clk(t_ff_1_qn), .Q(value[1]), .Qn(t_ff_2_qn), .reset(R));  // open: preset
  T_Flip_Flop t_ff_3 (.T(1'b1), .clk(t_ff_2_qn), .Q(value[2]), .Qn(t_ff_3_qn), .reset(R));  // open: preset
  T_Flip_Flop t_ff_4 (.T(1'b1), .clk(t_ff_3_qn), .Q(value[3]), .Qn(t_ff_4_qn), .reset(R));  // open: preset
  T_Flip_Flop t_ff_5 (.T(1'b1), .clk(t_ff_4_qn), .Q(value[4]), .Qn(t_ff_5_qn), .reset(R));  // open: preset
  T_Flip_Flop t_ff_6 (.T(1'b1), .clk(t_ff_5_qn), .Q(value[5]), .Qn(t_ff_6_qn), .reset(R));  // open: preset
  T_Flip_Flop t_ff_7 (.T(1'b1), .clk(t_ff_6_qn), .Q(value[6]), .Qn(t_ff_7_qn), .reset(R));  // open: preset
  T_Flip_Flop t_ff_8 (.T(1'b1), .clk(t_ff_7_qn), .Q(value[7]), .Qn(count_out), .reset(R));  // open: preset
endmodule

module count_32bit (
  input  clk,
  input  R,
  output [31:0] out_3,
  output count_out
);

  wire count_8bit_1_count_out, count_8bit_2_count_out, count_8bit_3_count_out;

  count_8bit count_8bit_1 (.clk(clk), .R(R), .value(out_3[7:0]), .count_out(count_8bit_1_count_out));
  count_8bit count_8bit_2 (
    .clk(count_8bit_1_count_out), .R(R), .value(out_3[15:8]), .count_out(count_8bit_2_count_out));
  count_8bit count_8bit_3 (
    .clk(count_8bit_2_count_out), .R(R), .value(out_3[23:16]), .count_out(count_8bit_3_count_out));
  count_8bit count_8bit_4 (.clk(count_8bit_3_count_out), .R(R), .value(out_3[31:24]), .count_out(count_out));
endmodule
